// Logisim project main.circ as structural Verilog: 4 circuits, main circuit main
module main (
  input  reset,
  input  WE,
  input  [2:0] WriteReg,
  input  [2:0] ReadReg1,
  input  [1:0] OpType,
  input  [2:0] ReadReg2
);

  wire clock_1_out;
  wire [15:0] alu_1_outputdata, registerfile_1_reg1contents, registerfile_1_reg2contents;

  Clock clock_1 (.out(clock_1_out));
  RegisterFile registerfile_1 (
    .clk(clock_1_out), .reset(reset), .WriteData(alu_1_outputdata), .RegWriteEnable(WE),
    .WritePort(WriteReg), .readReg1(ReadReg1), .readReg2(ReadReg2),
    .Reg1Contents(registerfile_1_reg1contents), .Reg2Contents(registerfile_1_reg2contents));  // open: readReg3, readReg4, readReg7, readReg8, readReg5, readReg6, Reg3Contents, Reg4Contents, Reg5Contents, Reg6Contents, Reg7Contents, Reg8Contents
  ALU alu_1 (
    .InputData1(registerfile_1_reg1contents), .InputData2(registerfile_1_reg2contents), .OpType(OpType),
    .OutputData(alu_1_outputdata));
endmodule

module singleRegister (
  input  [15:0] dataIn,
  input  clk,
  input  writeEnable,
  input  reset,
  output [15:0] dataOut
);

  wire clk_t;

  and and_1 (clk_t, clk, writeEnable);
  D_Flip_Flop d_ff_1 (.D(dataIn[0]), .clk(clk_t), .Q(dataOut[0]), .reset(reset));  // open: Qn, preset
  D_Flip_Flop d_ff_2 (.D(dataIn[1]), .clk(clk_t), .Q(dataOut[1]), .reset(reset));  // open: Qn, preset
  D_Flip_Flop d_ff_3 (.D(dataIn[2]), .clk(clk_t), .Q(dataOut[2]), .reset(reset));  // open: Qn, preset
  D_Flip_Flop d_ff_4 (.D(dataIn[3]), .clk(clk_t), .Q(dataOut[3]), .reset(reset));  // open: Qn, preset
  D_Flip_Flop d_ff_5 (.D(dataIn[4]), .clk(clk_t), .Q(dataOut[4]), .reset(reset));  // open: Qn, preset
  D_Flip_Flop d_ff_6 (.D(dataIn[5]), .clk(clk_t), .Q(dataOut[5]), .reset(reset));  // open: Qn, preset
  D_Flip_Flop d_ff_7 (.D(dataIn[6]), .clk(clk_t), .Q(dataOut[6]), .reset(reset));  // open: Qn, preset
  D_Flip_Flop d_ff_8 (.D(dataIn[7]), .clk(clk_t), .Q(dataOut[7]), .reset(reset));  // open: Qn, preset
  D_Flip_Flop d_ff_9 (.D(dataIn[8]), .clk(clk_t), .Q(dataOut[8]), .reset(reset));  // open: Qn, preset
  D_Flip_Flop d_ff_10 (.D(dataIn[9]), .clk(clk_t), .Q(dataOut[9]), .reset(reset));  // open: Qn, preset
  D_Flip_Flop d_ff_11 (.D(dataIn[10]), .clk(clk_t), .Q(dataOut[10]), .reset(reset));  // open: Qn, preset
  D_Flip_Flop d_ff_12 (.D(dataIn[11]), .clk(clk_t), .Q(dataOut[11]), .reset(reset));  // open: Qn, preset
  D_Flip_Flop d_ff_13 (.D(dataIn[12]), .clk(clk_t), .Q(dataOut[12]), .reset(reset));  // open: Qn, preset
  D_Flip_Flop d_ff_14 (.D(dataIn[13]), .clk(clk_t), .Q(dataOut[13]), .reset(reset));  // open: Qn, preset
  D_Flip_Flop d_ff_15 (.D(dataIn[14]), .clk(clk_t), .Q(dataOut[14]), .reset(reset));  // open: Qn, preset
  D_Flip_Flop d_ff_16 (.D(dataIn[15]), .clk(clk_t), .Q(dataOut[15]), .reset(reset));  // open: Qn, preset

  // Other names for the same wires on the sheet: in0 = dataIn[0]; in1 = dataIn[1]; in2 = dataIn[2]; in3 = dataIn[3];
  //   in4 = dataIn[4]; in5 = dataIn[5]; in6 = dataIn[6]; in7 = dataIn[7]; in8 = dataIn[8]; in9 = dataIn[9];
  //   in10 = dataIn[10]; in11 = dataIn[11]; in12 = dataIn[12]; in13 = dataIn[13]; in14 = dataIn[14];
  //   in15 = dataIn[15]; out0 = dataOut[0]; out1 = dataOut[1]; out2 = dataOut[2]; out3 = dataOut[3];
  //   out4 = dataOut[4]; out5 = dataOut[5]; out6 = dataOut[6]; out7 = dataOut[7]; out8 = dataOut[8];
  //   out9 = dataOut[9]; out10 = dataOut[10]; out11 = dataOut[11]; out12 = dataOut[12]; out13 = dataOut[13];
  //   out14 = dataOut[14]; out15 = dataOut[15]
endmodule

module RegisterFile (
  input  clk,
  input  reset,
  input  [15:0] WriteData,
  input  RegWriteEnable,
  input  [2:0] WritePort,
  input  [2:0] readReg1,
  input  [2:0] readReg2,
  input  [2:0] readReg3,
  input  [2:0] readReg4,
  input  [2:0] readReg7,
  input  [2:0] readReg8,
  input  [2:0] readReg5,
  input  [2:0] readReg6,
  output [15:0] Reg1Contents,
  output [15:0] Reg2Contents,
  output [15:0] Reg3Contents,
  output [15:0] Reg4Contents,
  output [15:0] Reg5Contents,
  output [15:0] Reg6Contents,
  output [15:0] Reg7Contents,
  output [15:0] Reg8Contents
);

  wire out1bit0, out1bit1, out2bit0, out2bit1, out3bit0, out3bit1, out4bit0, out4bit1, out5bit0, out5bit1,
       out6bit0, out6bit1, out7bit0, out7bit1, out8bit0, out8bit1, WE1;
  wire [15:0] controlled_buffer_5_out, singleregister_1_dataout;

  Decoder #(.select(3)) decoder_1 (
    .out1(WE1), .sel(WritePort), .en(RegWriteEnable));  // open: out0, out2, out3, out4, out5, out6, out7
  Decoder #(.select(3)) decoder_2 (
    .out0(out1bit0), .out1(out1bit1), .sel(readReg1));  // open: out2, out3, out4, out5, out6, out7, en
  Decoder #(.select(3)) decoder_3 (
    .out0(out5bit0), .out1(out5bit1), .sel(readReg5));  // open: out2, out3, out4, out5, out6, out7, en
  Decoder #(.select(3)) decoder_4 (
    .out0(out2bit0), .out1(out2bit1), .sel(readReg2));  // open: out2, out3, out4, out5, out6, out7, en
  Decoder #(.select(3)) decoder_5 (
    .out0(out6bit0), .out1(out6bit1), .sel(readReg6));  // open: out2, out3, out4, out5, out6, out7, en
  Decoder #(.select(3)) decoder_6 (
    .out0(out3bit0), .out1(out3bit1), .sel(readReg3));  // open: out2, out3, out4, out5, out6, out7, en
  Decoder #(.select(3)) decoder_7 (
    .out0(out7bit0), .out1(out7bit1), .sel(readReg7));  // open: out2, out3, out4, out5, out6, out7, en
  Decoder #(.select(3)) decoder_8 (
    .out0(out4bit0), .out1(out4bit1), .sel(readReg4));  // open: out2, out3, out4, out5, out6, out7, en
  Decoder #(.select(3)) decoder_9 (
    .out0(out8bit0), .out1(out8bit1), .sel(readReg8));  // open: out2, out3, out4, out5, out6, out7, en
  singleRegister singleregister_1 (
    .dataIn(WriteData), .clk(clk), .writeEnable(WE1), .reset(reset), .dataOut(singleregister_1_dataout));
  assign Reg2Contents = out2bit0 ? controlled_buffer_5_out : 16'bz;  // Controlled_Buffer controlled_buffer_1
  assign Reg2Contents = out2bit1 ? singleregister_1_dataout : 16'bz;  // Controlled_Buffer controlled_buffer_2
  assign Reg1Contents = out1bit0 ? controlled_buffer_5_out : 16'bz;  // Controlled_Buffer controlled_buffer_3
  assign Reg1Contents = out1bit1 ? singleregister_1_dataout : 16'bz;  // Controlled_Buffer controlled_buffer_4
  assign controlled_buffer_5_out = out4bit1 ? singleregister_1_dataout : 16'bz;  // Controlled_Buffer controlled_buffer_5
  assign Reg6Contents = out6bit0 ? controlled_buffer_5_out : 16'bz;  // Controlled_Buffer controlled_buffer_6
  assign Reg5Contents = out5bit0 ? controlled_buffer_5_out : 16'bz;  // Controlled_Buffer controlled_buffer_7
  assign Reg7Contents = out7bit0 ? controlled_buffer_5_out : 16'bz;  // Controlled_Buffer controlled_buffer_8
  assign Reg8Contents = out8bit0 ? controlled_buffer_5_out : 16'bz;  // Controlled_Buffer controlled_buffer_9
  assign controlled_buffer_5_out = out3bit1 ? singleregister_1_dataout : 16'bz;  // Controlled_Buffer controlled_buffer_10
  assign Reg3Contents = out3bit0 ? controlled_buffer_5_out : 16'bz;  // Controlled_Buffer controlled_buffer_11
  assign Reg5Contents = out5bit1 ? singleregister_1_dataout : 16'bz;  // Controlled_Buffer controlled_buffer_12
  assign Reg8Contents = out8bit1 ? singleregister_1_dataout : 16'bz;  // Controlled_Buffer controlled_buffer_13
  assign Reg4Contents = out4bit0 ? controlled_buffer_5_out : 16'bz;  // Controlled_Buffer controlled_buffer_14
  assign Reg6Contents = out6bit1 ? singleregister_1_dataout : 16'bz;  // Controlled_Buffer controlled_buffer_15
  assign Reg7Contents = out7bit1 ? singleregister_1_dataout : 16'bz;  // Controlled_Buffer controlled_buffer_16
  // also tied to GND on the sheet: {controlled_buffer_5_out[0], controlled_buffer_5_out[1], controlled_buffer_5_out[2], controlled_buffer_5_out[3], controlled_buffer_5_out[4], controlled_buffer_5_out[5], controlled_buffer_5_out[6], controlled_buffer_5_out[7], controlled_buffer_5_out[8], controlled_buffer_5_out[9], controlled_buffer_5_out[10], controlled_buffer_5_out[11], controlled_buffer_5_out[12], controlled_buffer_5_out[13], controlled_buffer_5_out[14], controlled_buffer_5_out[15]}
endmodule

module ALU (
  input  [15:0] InputData1,
  input  [15:0] InputData2,
  input  [1:0] OpType,
  output [15:0] OutputData
);

  wire [15:0] adder_1_out, not_1_out, or_1_out, subtractor_1_out;

  Adder #(.width(16)) adder_1 (.a(InputData1), .b(InputData2), .out(adder_1_out));  // open: cin, cout
  Subtractor #(.width(16)) subtractor_1 (.a(InputData1), .b(InputData2), .out(subtractor_1_out));  // open: bin, bout
  assign or_1_out = InputData1 | InputData2;  // OR_Gate or_1, 16 bits wide
  assign not_1_out = ~InputData1;  // NOT_Gate not_1, 16 bits wide
  Multiplexer #(.select(2), .width(16), .enable("false")) multiplexer_1 (
    .in0(adder_1_out), .in1(subtractor_1_out), .in2(or_1_out), .in3(not_1_out), .out(OutputData), .sel(OpType));
endmodule
