// Logisim project singleRegister.circ as structural Verilog
module singleRegister (
  input  [15:0] dataIn,
  input  clk,
  input  writeEnable,
  input  reset,
  output [15:0] dataOut
);

  wire clk_t;

  and and_1 (clk_t, clk, writeEnable);
  D_Flip_Flop d_ff_1 (.D(dataIn[0]), .clk(clk_t), .Q(dataOut[0]), .reset(reset));  // open: Qn, preset
  D_Flip_Flop d_ff_2 (.D(dataIn[1]), .clk(clk_t), .Q(dataOut[1]), .reset(reset));  // open: Qn, preset
  D_Flip_Flop d_ff_3 (.D(dataIn[2]), .clk(clk_t), .Q(dataOut[2]), .reset(reset));  // open: Qn, preset
  D_Flip_Flop d_ff_4 (.D(dataIn[3]), .clk(clk_t), .Q(dataOut[3]), .reset(reset));  // open: Qn, preset
  D_Flip_Flop d_ff_5 (.D(dataIn[4]), .clk(clk_t), .Q(dataOut[4]), .reset(reset));  // open: Qn, preset
  D_Flip_Flop d_ff_6 (.D(dataIn[5]), .clk(clk_t), .Q(dataOut[5]), .reset(reset));  // open: Qn, preset
  D_Flip_Flop d_ff_7 (.D(dataIn[6]), .clk(clk_t), .Q(dataOut[6]), .reset(reset));  // open: Qn, preset
  D_Flip_Flop d_ff_8 (.D(dataIn[7]), .clk(clk_t), .Q(dataOut[7]), .reset(reset));  // open: Qn, preset
  D_Flip_Flop d_ff_9 (.D(dataIn[8]), .clk(clk_t), .Q(dataOut[8]), .reset(reset));  // open: Qn, preset
  D_Flip_Flop d_ff_10 (.D(dataIn[9]), .clk(clk_t), .Q(dataOut[9]), .reset(reset));  // open: Qn, preset
  D_Flip_Flop d_ff_11 (.D(dataIn[10]), .clk(clk_t), .Q(dataOut[10]), .reset(reset));  // open: Qn, preset
  D_Flip_Flop d_ff_12 (.D(dataIn[11]), .clk(clk_t), .Q(dataOut[11]), .reset(reset));  // open: Qn, preset
  D_Flip_Flop d_ff_13 (.D(dataIn[12]), .clk(clk_t), .Q(dataOut[12]), .reset(reset));  // open: Qn, preset
  D_Flip_Flop d_ff_14 (.D(dataIn[13]), .clk(clk_t), .Q(dataOut[13]), .reset(reset));  // open: Qn, preset
  D_Flip_Flop d_ff_15 (.D(dataIn[14]), .clk(clk_t), .Q(dataOut[14]), .reset(reset));  // open: Qn, preset
  D_Flip_Flop d_ff_16 (.D(dataIn[15]), .clk(clk_t), .Q(dataOut[15]), .reset(reset));  // open: Qn, preset

  // Other names for the same wires on the sheet: in0 = dataIn[0]; in1 = dataIn[1]; in2 = dataIn[2]; in3 = dataIn[3];
  //   in4 = dataIn[4]; in5 = dataIn[5]; in6 = dataIn[6]; in7 = dataIn[7]; in8 = dataIn[8]; in9 = dataIn[9];
  //   in10 = dataIn[10]; in11 = dataIn[11]; in12 = dataIn[12]; in13 = dataIn[13]; in14 = dataIn[14];
  //   in15 = dataIn[15]; out0 = dataOut[0]; out1 = dataOut[1]; out2 = dataOut[2]; out3 = dataOut[3];
  //   out4 = dataOut[4]; out5 = dataOut[5]; out6 = dataOut[6]; out7 = dataOut[7]; out8 = dataOut[8];
  //   out9 = dataOut[9]; out10 = dataOut[10]; out11 = dataOut[11]; out12 = dataOut[12]; out13 = dataOut[13];
  //   out14 = dataOut[14]; out15 = dataOut[15]
endmodule

module RegisterFile (
  input  clk,
  input  reset,
  input  [15:0] WriteData,
  input  RegWriteEnable,
  input  [2:0] WritePort,
  input  [2:0] readReg1,
  input  [2:0] readReg2,
  input  [2:0] readReg3,
  input  [2:0] readReg4,
  input  [2:0] readReg7,
  input  [2:0] readReg8,
  input  [2:0] readReg5,
  input  [2:0] readReg6,
  output [15:0] Reg1Contents,
  output [15:0] Reg2Contents,
  output [15:0] Reg3Contents,
  output [15:0] out_17,
  output [15:0] out_18,
  output [15:0] out_19,
  output [15:0] out_20,
  output [15:0] out_21
);

  wire out1bit0, out1bit1, out2bit0, out2bit1, out3bit0, out3bit1, out4bit0, out4bit1, out5bit0, out5bit1,
       out6bit0, out6bit1, out7bit0, out7bit1, out8bit0, out8bit1, WE1;
  wire [15:0] singleregister_1_dataout;

  Decoder #(.select(3)) decoder_1 (
    .out1(WE1), .sel(WritePort), .en(RegWriteEnable));  // open: out0, out2, out3, out4, out5, out6, out7
  Decoder #(.select(3)) decoder_2 (
    .out0(out1bit0), .out1(out1bit1), .sel(readReg1));  // open: out2, out3, out4, out5, out6, out7, en
  Decoder #(.select(3)) decoder_3 (
    .out0(out5bit0), .out1(out5bit1), .sel(readReg5));  // open: out2, out3, out4, out5, out6, out7, en
  Decoder #(.select(3)) decoder_4 (
    .out0(out2bit0), .out1(out2bit1), .sel(readReg2));  // open: out2, out3, out4, out5, out6, out7, en
  Decoder #(.select(3)) decoder_5 (
    .out0(out6bit0), .out1(out6bit1), .sel(readReg6));  // open: out2, out3, out4, out5, out6, out7, en
  Decoder #(.select(3)) decoder_6 (
    .out0(out3bit0), .out1(out3bit1), .sel(readReg3));  // open: out2, out3, out4, out5, out6, out7, en
  Decoder #(.select(3)) decoder_7 (
    .out0(out7bit0), .out1(out7bit1), .sel(readReg7));  // open: out2, out3, out4, out5, out6, out7, en
  Decoder #(.select(3)) decoder_8 (
    .out0(out4bit0), .out1(out4bit1), .sel(readReg4));  // open: out2, out3, out4, out5, out6, out7, en
  Decoder #(.select(3)) decoder_9 (
    .out0(out8bit0), .out1(out8bit1), .sel(readReg8));  // open: out2, out3, out4, out5, out6, out7, en
  singleRegister singleregister_1 (
    .dataIn(WriteData), .clk(clk), .writeEnable(WE1), .reset(reset), .dataOut(singleregister_1_dataout));
  assign Reg2Contents = out2bit0 ? {16{1'b0}} : 16'bz;  // Controlled_Buffer controlled_buffer_1
  assign Reg2Contents = out2bit1 ? singleregister_1_dataout : 16'bz;  // Controlled_Buffer controlled_buffer_2
  assign Reg1Contents = out1bit0 ? {16{1'b0}} : 16'bz;  // Controlled_Buffer controlled_buffer_3
  assign Reg1Contents = out1bit1 ? singleregister_1_dataout : 16'bz;  // Controlled_Buffer controlled_buffer_4
  assign Reg1Contents = out4bit1 ? singleregister_1_dataout : 16'bz;  // Controlled_Buffer controlled_buffer_5
  assign out_19 = out6bit0 ? Reg1Contents : 16'bz;  // Controlled_Buffer controlled_buffer_6
  assign out_18 = out5bit0 ? Reg1Contents : 16'bz;  // Controlled_Buffer controlled_buffer_7
  assign out_20 = out7bit0 ? Reg1Contents : 16'bz;  // Controlled_Buffer controlled_buffer_8
  assign out_21 = out8bit0 ? Reg1Contents : 16'bz;  // Controlled_Buffer controlled_buffer_9
  assign Reg1Contents = out3bit1 ? singleregister_1_dataout : 16'bz;  // Controlled_Buffer controlled_buffer_10
  assign Reg3Contents = out3bit0 ? Reg1Contents : 16'bz;  // Controlled_Buffer controlled_buffer_11
  assign out_18 = out5bit1 ? singleregister_1_dataout : 16'bz;  // Controlled_Buffer controlled_buffer_12
  assign out_21 = out8bit1 ? singleregister_1_dataout : 16'bz;  // Controlled_Buffer controlled_buffer_13
  assign out_17 = out4bit0 ? Reg1Contents : 16'bz;  // Controlled_Buffer controlled_buffer_14
  assign out_19 = out6bit1 ? singleregister_1_dataout : 16'bz;  // Controlled_Buffer controlled_buffer_15
  assign out_20 = out7bit1 ? singleregister_1_dataout : 16'bz;  // Controlled_Buffer controlled_buffer_16
endmodule
